# Fritzing sketch sketch (saved by Fritzing 0.9.3b)
breadboards: 1

parts:
  Potenciometro_B50K = POT [package=pot_alpha_rv16af-20]
  Transitor_2N2222A = TRANSISTOR_NPN_2 [package=to-92]
  M1 = DC Motor
  VCC1 = Battery block 9V

nets:
  N1: Potenciometro_B50K.A, Transitor_2N2222A.C, M1.pin_2
  N2: Potenciometro_B50K.S, Transitor_2N2222A.B
  N3: Potenciometro_B50K.E, Transitor_2N2222A.E, VCC1.+
  N4: M1.pin_1, VCC1.-

notes:
  rojo:Positivo(+)
  negro:Negativo(-)
